# Fritzing sketch Arduino Mega + HC-05 (saved by Fritzing 0.9.3b)

parts:
  Part1 = Bluetooth HC-05 Macho
  Part2 = Arduino Mega 2560 (Rev3)
  4_Channel_Relay1 = 4 Channel Power Relay

nets:
  N1: Part1.TXD, Part2.D19/RX1
  VCC: Part1.VCC, Part2.5V, 4_Channel_Relay1.VCC
  GND: Part1.GND, Part2.GND, 4_Channel_Relay1.GND
  N2: Part2.A0, 4_Channel_Relay1.IN4
  N3: Part2.A1, 4_Channel_Relay1.IN3
  N4: Part2.A2, 4_Channel_Relay1.IN2
  N5: Part2.A3, 4_Channel_Relay1.IN1

notes:
  โมดูลบลูทูธ
  บอร์ด Arduino Mega 2560
  โมดูลรีเลย์

custom parts:
  4 Channel Power Relay: A 4 channel power relay. The module operates at 5V.
